# Fritzing sketch FastLED_Demo1 (saved by Fritzing 0.9.3b)
breadboards: 1

parts:
  Part1 = Arduino Uno (Rev3)
  Power_plug1 = Power plug
  C1 = Electrolytic Capacitor [capacitance=1mF voltage=50V package="100 mil [THT, electrolytic]"]
  NEOPIXEL1 = Neopixel Strip -- White (60/m)

nets:
  N1: Part1.D3_PWM, NEOPIXEL1.DI
  GND: Part1.GND, Power_plug1.GND, C1.+, NEOPIXEL1.GND
  VCC: Power_plug1.VCC, C1.-, NEOPIXEL1.+5V

custom parts:
  Neopixel Strip -- White (60/m): Neopixel Strip, White, 60 pixels per meter.
